// Logisim project initial_labs.circ as structural Verilog: 1 circuit, main circuit x3plus6
module x3plus6 (
  input  A,
  input  B,
  output A_OR_B,
  output A_OR_nB,
  output A_XNOR_B,
  output B_2
);

  wire not_1_out;

  not not_1 (not_1_out, B);
  or or_1 (A_OR_B, A, B);
  or or_2 (A_OR_nB, A, not_1_out);
  xnor xnor_1 (A_XNOR_B, A, B);

  assign B_2 = B;

  // Notes on the sheet:
  //   Lab #1
  //   initial_labs.circ
  //   William Hampton
endmodule
